// Logisim project 16x16mult_PCU.circ as structural Verilog: 7 circuits, main circuit main
module main (
);

  wire and_1_out, and_2_out, and_3_out, and_4_out, and_5_out, and_6_out, and_7_out, and_8_out, and_9_out,
       and_10_out, and_11_out, and_12_out, and_13_out, and_14_out, and_15_out, and_16_out, and_17_out,
       and_18_out, clock_1_out, comparator_1_eq, comparator_2_eq, comparator_3_eq, comparator_4_eq,
       comparator_5_eq, comparator_6_eq, comparator_7_eq, comparator_8_eq, comparator_9_eq, comparator_10_eq,
       comparator_11_eq, decoder_1_out0, decoder_1_out1, decoder_1_out2, decoder_1_out3, decoder_2_out0,
       decoder_2_out1, decoder_2_out2, decoder_2_out3, decoder_3_out0, decoder_3_out1, decoder_3_out2,
       decoder_3_out3, ldecoder_1_a11, ldecoder_1_a12, ldecoder_1_a21, ldecoder_1_a22, ldecoder_1_a31,
       ldecoder_1_a32, ldecoder_1_a41, ldecoder_1_a42, ldecoder_1_a51, ldecoder_1_a52, ldecoder_1_a61,
       ldecoder_1_a62, ldecoder_1_a71, ldecoder_1_a72, ldecoder_1_a81, ldecoder_1_a82, ldecoder_2_a11,
       ldecoder_2_a12, ldecoder_2_a21, ldecoder_2_a22, ldecoder_2_a31, ldecoder_2_a32, ldecoder_2_a41,
       ldecoder_2_a42, ldecoder_2_a51, ldecoder_2_a52, ldecoder_2_a61, ldecoder_2_a62, ldecoder_2_a71,
       ldecoder_2_a72, ldecoder_2_a81, ldecoder_2_a82, not_1_out, not_2_out, not_3_out, not_4_out, not_5_out,
       not_6_out, not_7_out, or_1_out, or_2_out, or_3_out, register_1_q, register_2_q, register_5_q,
       register_8_q, register_9_q, register_10_q, register_11_q, register_12_q, register_13_q, xor_1_out;
  wire [1:0] rom_1_data_2;
  wire [2:0] counter_1_q;
  wire [3:0] adder_10_out, controlled_buffer_13_out, flag_q, inst_decoder_1_flag, inst_decoder_1_opcode;
  wire [7:0] controlled_buffer_1_out, controlled_buffer_2_out, MAR_inst_q, PC_q, subtractor_1_out;
  wire [9:0] adder_2_out, adder_3_out, adder_4_out, adder_5_out, adder_6_out, adder_7_out, adder_8_out,
       adder_9_out, adder_11_out, adder_12_out, adder_13_out, adder_14_out, adder_15_out, bit_extender_1_out,
       BS_address_control_q, column_counter_q, controlled_buffer_3_out, controlled_buffer_4_out,
       divider_1_out, divider_2_out, divider_3_out, execution_address_control_q, inst_decoder_1_add_a,
       inst_decoder_1_add_b, MAR_A_q, MAR_B_q, multiplier_1_out, multiplier_2_out, multiplier_3_out,
       multiplier_4_out, multiplier_5_out, multiplier_6_out, multiplier_7_out, outerDimA_q, outerDimB_q,
       row_counter_q, step_counter_q, x_counter_q, y_counter_q;
  wire [11:0] counter_2_q;
  wire [15:0] clock_cycle_counter_q, counter_3_q, counter_4_q, counter_5_q, register_14_q, register_15_q,
       register_16_q, register_17_q, register_18_q, register_19_q, register_20_q, register_21_q,
       register_22_q, register_23_q, register_24_q, register_25_q;
  wire [27:0] mbr_instr_q, RAM_inst_dout;
  wire [63:0] A11_q, A12_q, A13_q, A14_q, A21_q, A22_q, A23_q, A24_q, A31_q, A32_q, A33_q, A34_q, A41_q,
       A42_q, A43_q, A44_q, A51_q, A52_q, A53_q, A54_q, A61_q, A62_q, A63_q, A64_q, A71_q, A72_q, A73_q,
       A74_q, A81_q, A82_q, A83_q, A84_q, B11_q, B12_q, B13_q, B14_q, B21_q, B22_q, B23_q, B24_q, B31_q,
       B32_q, B33_q, B34_q, B41_q, B42_q, B43_q, B44_q, B51_q, B52_q, B53_q, B54_q, B61_q, B62_q, B63_q,
       B64_q, B71_q, B72_q, B73_q, B74_q, B81_q, B82_q, B83_q, B84_q, C1_dout, C2_dout, C3_dout, C4_dout,
       controlled_buffer_9_out, core16x16_1_s1, core16x16_1_s2, core16x16_1_s3, core16x16_1_s4, ramA1_dout,
       ramA2_dout, ramB1_dout, ramB2_dout, register_3_q, register_4_q, register_6_q, register_7_q, rom_1_data;

  and and_1 (and_1_out, comparator_2_eq, comparator_1_eq);
  Subtractor subtractor_1 (.a(PC_q), .b(8'h2), .out(subtractor_1_out));  // open: bin, bout
  assign controlled_buffer_1_out = not_1_out ? subtractor_1_out : 8'bz;  // Controlled_Buffer controlled_buffer_1
  assign controlled_buffer_2_out = and_1_out ? PC_q : 8'bz;  // Controlled_Buffer controlled_buffer_2
  not not_1 (not_1_out, and_1_out);
  Comparator #(.mode("unsigned"), .width(10)) comparator_1 (
    .a({10{1'b0}}), .b(row_counter_q), .eq(comparator_1_eq));  // open: gt, lt
  Adder adder_1 (.a(controlled_buffer_2_out), .b(8'h1), .out(controlled_buffer_1_out));  // open: cin, cout
  or or_1 (or_1_out, and_7_out, rom_1_data[61]);
  and and_2 (and_2_out, comparator_3_eq, comparator_9_eq);
  Comparator #(.mode("unsigned"), .width(10)) comparator_2 (
    .a({10{1'b0}}), .b(column_counter_q), .eq(comparator_2_eq));  // open: gt, lt
  Counter PC (
    .load(rom_1_data[57]), .up(or_1_out), .count(or_1_out), .clk(clock_1_out), .D(controlled_buffer_1_out),
    .Q(PC_q));  // open: clr, carry
  Register #(.width(1)) register_1 (.D(and_5_out), .en(1'b1), .clk(clock_1_out), .Q(register_1_q));  // open: clr
  // Probe on PC_q
  Counter #(.max('h3ff), .width(10)) BS_address_control (
    .count(decoder_1_out3), .clk(clock_1_out), .Q(BS_address_control_q));  // open: clr, load, up, D, carry
  Counter #(.max('h3ff), .width(10)) execution_address_control (
    .up(rom_1_data[44]), .count(rom_1_data[44]), .clk(clock_1_out), .Q(execution_address_control_q));  // open: clr, load, D, carry
  Register #(.width(1)) register_2 (.D(comparator_3_eq), .en(1'b1), .clk(clock_1_out), .Q(register_2_q));  // open: clr
  Counter #(.max('h3ff), .width(10)) x_counter (
    .clr(register_2_q), .count(decoder_1_out3), .clk(clock_1_out), .Q(x_counter_q));  // open: load, up, D, carry
  Counter #(.max('h3ff), .width(10)) y_counter (
    .clr(register_1_q), .count(and_2_out), .clk(clock_1_out), .Q(y_counter_q));  // open: load, up, D, carry
  Register MAR_inst (.D(PC_q), .en(rom_1_data[60]), .clk(clock_1_out), .Q(MAR_inst_q));  // open: clr
  Register #(.width(64)) A11 (.D(ramA1_dout), .en(and_8_out), .clk(clock_1_out), .Q(A11_q), .clr(rom_1_data[8]));
  Register #(.width(64)) A21 (.D(ramA1_dout), .en(ldecoder_1_a21), .clk(clock_1_out), .Q(A21_q), .clr(rom_1_data[8]));
  Register #(.width(64)) A31 (.D(ramA1_dout), .en(ldecoder_1_a31), .clk(clock_1_out), .Q(A31_q), .clr(rom_1_data[8]));
  Register #(.width(64)) A41 (.D(ramA1_dout), .en(ldecoder_1_a41), .clk(clock_1_out), .Q(A41_q), .clr(rom_1_data[8]));
  Register #(.width(64)) A51 (.D(ramA1_dout), .en(ldecoder_1_a51), .clk(clock_1_out), .Q(A51_q), .clr(rom_1_data[8]));
  Register #(.width(64)) A61 (.D(ramA1_dout), .en(ldecoder_1_a61), .clk(clock_1_out), .Q(A61_q), .clr(rom_1_data[8]));
  Register #(.width(64)) A71 (.D(ramA1_dout), .en(ldecoder_1_a71), .clk(clock_1_out), .Q(A71_q), .clr(rom_1_data[8]));
  Register #(.width(64)) A81 (.D(ramA1_dout), .en(ldecoder_1_a81), .clk(clock_1_out), .Q(A81_q), .clr(rom_1_data[8]));
  and and_3 (and_3_out, comparator_8_eq, rom_1_data[50]);
  Multiplier #(.width(10)) multiplier_1 (.a(x_counter_q), .b(10'h2), .out(multiplier_1_out));  // open: cin, cout
  Comparator #(.mode("unsigned"), .width(10)) comparator_3 (
    .a(x_counter_q), .b(divider_1_out), .eq(comparator_3_eq));  // open: gt, lt
  Divider #(.width(10)) divider_1 (.a(adder_14_out), .b(10'h2), .out(divider_1_out));  // open: upper, rem
  RAM #(.dataWidth(28), .\type ("nonvolatile")) RAM_inst (
    .addr(MAR_inst_q), .oe(rom_1_data[60]), .clk(clock_1_out), .dout(RAM_inst_dout));  // open: we, din
  and and_4 (and_4_out, comparator_5_eq, comparator_8_eq);
  Counter #(.max('h3ff), .width(10)) row_counter (
    .clr(and_4_out), .up(comparator_8_eq), .count(comparator_8_eq), .clk(clock_1_out), .Q(row_counter_q));  // open: load, D, carry
  Adder #(.width(10)) adder_2 (.a(MAR_A_q), .b(multiplier_1_out), .out(adder_2_out));  // open: cin, cout
  Multiplier #(.width(10)) multiplier_2 (.a(y_counter_q), .b(10'h2), .out(multiplier_2_out));  // open: cin, cout
  Comparator #(.mode("unsigned"), .width(10)) comparator_4 (
    .a(y_counter_q), .b(divider_3_out), .eq(comparator_4_eq));  // open: gt, lt
  Multiplier #(.width(10)) multiplier_3 (
    .a(adder_14_out), .b(multiplier_2_out), .out(multiplier_3_out));  // open: cin, cout
  and and_5 (and_5_out, register_2_q, comparator_4_eq);
  Register #(.width(64)) A12 (.D(ramA1_dout), .en(ldecoder_1_a12), .clk(clock_1_out), .Q(A12_q), .clr(rom_1_data[8]));
  Register #(.width(64)) A22 (.D(ramA1_dout), .en(ldecoder_1_a22), .clk(clock_1_out), .Q(A22_q), .clr(rom_1_data[8]));
  Register #(.width(64)) A32 (.D(ramA1_dout), .en(ldecoder_1_a32), .clk(clock_1_out), .Q(A32_q), .clr(rom_1_data[8]));
  Register #(.width(64)) A42 (.D(ramA1_dout), .en(ldecoder_1_a42), .clk(clock_1_out), .Q(A42_q), .clr(rom_1_data[8]));
  Register #(.width(64)) A52 (.D(ramA1_dout), .en(ldecoder_1_a52), .clk(clock_1_out), .Q(A52_q), .clr(rom_1_data[8]));
  Adder #(.width(10)) adder_3 (.a(adder_2_out), .b(multiplier_3_out), .out(adder_3_out));  // open: cin, cout
  Adder #(.width(10)) adder_4 (.a(adder_3_out), .b(10'h1), .out(adder_4_out));  // open: cin, cout
  Adder #(.width(10)) adder_5 (.a(adder_3_out), .b(adder_14_out), .out(adder_5_out));  // open: cin, cout
  Adder #(.width(10)) adder_6 (.a(adder_5_out), .b(10'h1), .out(adder_6_out));  // open: cin, cout
  // Probe on RAM_inst_dout
  Comparator #(.mode("unsigned"), .width(10)) comparator_5 (
    .a(divider_3_out), .b(row_counter_q), .eq(comparator_5_eq));  // open: gt, lt
  Multiplier #(.width(10)) multiplier_4 (.a(10'h2), .b(row_counter_q), .out(multiplier_4_out));  // open: cin, cout
  Register #(.width(64)) A62 (.D(ramA1_dout), .en(ldecoder_1_a62), .clk(clock_1_out), .Q(A62_q), .clr(rom_1_data[8]));
  Register #(.width(64)) A72 (.D(ramA1_dout), .en(ldecoder_1_a72), .clk(clock_1_out), .Q(A72_q), .clr(rom_1_data[8]));
  Register #(.width(64)) A82 (.D(ramA1_dout), .en(ldecoder_1_a82), .clk(clock_1_out), .Q(A82_q), .clr(rom_1_data[8]));
  Comparator #(.mode("unsigned"), .width(4)) comparator_6 (
    .a(counter_2_q[11:8]), .b(4'b0100), .eq(comparator_6_eq));  // open: gt, lt
  assign controlled_buffer_3_out = comparator_6_eq ? BS_address_control_q : 10'bz;  // Controlled_Buffer controlled_buffer_3
  Decoder #(.select(2)) decoder_1 (
    .out0(decoder_1_out0), .out1(decoder_1_out1), .out2(decoder_1_out2), .out3(decoder_1_out3),
    .sel(rom_1_data_2));  // open: en
  assign controlled_buffer_4_out = decoder_1_out0 ? adder_3_out : 10'bz;  // Controlled_Buffer controlled_buffer_4
  assign controlled_buffer_4_out = decoder_1_out1 ? adder_4_out : 10'bz;  // Controlled_Buffer controlled_buffer_5
  assign controlled_buffer_4_out = decoder_1_out2 ? adder_5_out : 10'bz;  // Controlled_Buffer controlled_buffer_6
  assign controlled_buffer_4_out = decoder_1_out3 ? adder_6_out : 10'bz;  // Controlled_Buffer controlled_buffer_7
  Register #(.width(28)) mbr_instr (
    .D(RAM_inst_dout), .en(rom_1_data[39]), .clk(clock_1_out), .Q(mbr_instr_q));  // open: clr
  Adder #(.width(10)) adder_7 (.a(MAR_A_q), .b(step_counter_q), .out(adder_7_out));  // open: cin, cout
  Multiplier #(.width(10)) multiplier_5 (
    .a(bit_extender_1_out), .b(multiplier_4_out), .out(multiplier_5_out));  // open: cin, cout
  not not_2 (not_2_out, comparator_6_eq);
  assign controlled_buffer_3_out = not_2_out ? execution_address_control_q : 10'bz;  // Controlled_Buffer controlled_buffer_8
  Adder #(.width(10)) adder_8 (.a(adder_7_out), .b(multiplier_5_out), .out(adder_8_out));  // open: cin, cout
  not not_3 (not_3_out, comparator_7_eq);
  Register #(.width(64)) A13 (.D(ramA2_dout), .en(and_8_out), .clk(clock_1_out), .Q(A13_q), .clr(rom_1_data[8]));
  Register #(.width(64)) A23 (.D(ramA2_dout), .en(ldecoder_1_a21), .clk(clock_1_out), .Q(A23_q), .clr(rom_1_data[8]));
  Register #(.width(64)) A33 (.D(ramA2_dout), .en(ldecoder_1_a31), .clk(clock_1_out), .Q(A33_q), .clr(rom_1_data[8]));
  RAM #(.addrWidth(10), .dataWidth(64), .\type ("nonvolatile")) ramA1 (
    .addr(adder_8_out), .oe(and_6_out), .clk(clock_1_out), .dout(ramA1_dout));  // open: we, din
  and and_6 (and_6_out, not_3_out, rom_1_data[54]);
  Register #(.width(64)) A43 (.D(ramA2_dout), .en(ldecoder_1_a41), .clk(clock_1_out), .Q(A43_q), .clr(rom_1_data[8]));
  Register #(.width(64)) A53 (.D(ramA2_dout), .en(ldecoder_1_a51), .clk(clock_1_out), .Q(A53_q), .clr(rom_1_data[8]));
  Register #(.width(64)) A63 (.D(ramA2_dout), .en(ldecoder_1_a61), .clk(clock_1_out), .Q(A63_q), .clr(rom_1_data[8]));
  Register #(.width(64)) A73 (.D(ramA2_dout), .en(ldecoder_1_a71), .clk(clock_1_out), .Q(A73_q), .clr(rom_1_data[8]));
  Register #(.width(64)) A83 (.D(ramA2_dout), .en(ldecoder_1_a81), .clk(clock_1_out), .Q(A83_q), .clr(rom_1_data[8]));
  RAM #(.addrWidth(10), .dataWidth(64)) C1 (
    .addr(controlled_buffer_3_out), .we(rom_1_data[49]), .oe(rom_1_data[46]), .clk(clock_1_out),
    .din(core16x16_1_s1), .dout(C1_dout));
  Decoder #(.select(2)) decoder_2 (
    .out0(decoder_2_out0), .out1(decoder_2_out1), .out2(decoder_2_out2), .out3(decoder_2_out3),
    .sel(rom_1_data_2));  // open: en
  assign controlled_buffer_9_out = decoder_2_out1 ? register_4_q : 64'bz;  // Controlled_Buffer controlled_buffer_9
  inst_decoder inst_decoder_1 (
    .instruction(mbr_instr_q), .flag(inst_decoder_1_flag), .opcode(inst_decoder_1_opcode),
    .add_A(inst_decoder_1_add_a), .add_B(inst_decoder_1_add_b));
  Register #(.width(64)) register_3 (
    .D(C1_dout), .en(rom_1_data[45]), .clk(clock_1_out), .Q(register_3_q));  // open: clr
  assign controlled_buffer_9_out = decoder_2_out0 ? register_3_q : 64'bz;  // Controlled_Buffer controlled_buffer_10
  assign controlled_buffer_9_out = decoder_2_out2 ? register_6_q : 64'bz;  // Controlled_Buffer controlled_buffer_11
  assign controlled_buffer_9_out = decoder_2_out3 ? register_7_q : 64'bz;  // Controlled_Buffer controlled_buffer_12
  Register #(.width(64)) A14 (.D(ramA2_dout), .en(ldecoder_1_a12), .clk(clock_1_out), .Q(A14_q), .clr(rom_1_data[8]));
  Register #(.width(64)) A24 (.D(ramA2_dout), .en(ldecoder_1_a22), .clk(clock_1_out), .Q(A24_q), .clr(rom_1_data[8]));
  Register #(.width(64)) A34 (.D(ramA2_dout), .en(ldecoder_1_a32), .clk(clock_1_out), .Q(A34_q), .clr(rom_1_data[8]));
  Register #(.width(64)) A44 (.D(ramA2_dout), .en(ldecoder_1_a42), .clk(clock_1_out), .Q(A44_q), .clr(rom_1_data[8]));
  Register #(.width(64)) A54 (.D(ramA2_dout), .en(ldecoder_1_a52), .clk(clock_1_out), .Q(A54_q), .clr(rom_1_data[8]));
  Register #(.width(64)) A64 (.D(ramA2_dout), .en(ldecoder_1_a62), .clk(clock_1_out), .Q(A64_q), .clr(rom_1_data[8]));
  Register #(.width(64)) A74 (.D(ramA2_dout), .en(ldecoder_1_a72), .clk(clock_1_out), .Q(A74_q), .clr(rom_1_data[8]));
  and and_7 (and_7_out, and_5_out, comparator_9_eq);
  not not_4 (not_4_out, and_7_out);
  Adder #(.width(10)) adder_9 (.a(bit_extender_1_out), .b(adder_8_out), .out(adder_9_out));  // open: cin, cout
  Register #(.width(64)) A84 (.D(ramA2_dout), .en(ldecoder_1_a82), .clk(clock_1_out), .Q(A84_q), .clr(rom_1_data[8]));
  RAM #(.addrWidth(10), .dataWidth(64)) C2 (
    .addr(controlled_buffer_3_out), .we(rom_1_data[49]), .oe(rom_1_data[46]), .clk(clock_1_out),
    .din(core16x16_1_s2), .dout(C2_dout));
  assign controlled_buffer_13_out = and_7_out ? 4'b0000 : 4'bz;  // Controlled_Buffer controlled_buffer_13
  assign controlled_buffer_13_out = not_4_out ? inst_decoder_1_opcode : 4'bz;  // Controlled_Buffer controlled_buffer_14
  or or_2 (or_2_out, rom_1_data[59], comparator_9_eq, comparator_7_eq);
  RAM #(.addrWidth(10), .dataWidth(64), .\type ("nonvolatile")) ramA2 (
    .addr(adder_9_out), .oe(and_6_out), .clk(clock_1_out), .dout(ramA2_dout));  // open: we, din
  // Probe on core16x16_1_s2
  Register #(.width(4)) flag (
    .D(inst_decoder_1_flag), .en(rom_1_data[58]), .clk(clock_1_out), .Q(flag_q));  // open: clr
  Register #(.width(4)) opcode (
    .D(controlled_buffer_13_out), .en(or_2_out), .clk(clock_1_out), .Q(counter_2_q[11:8]));  // open: clr
  Register #(.width(10)) MAR_A (
    .D(inst_decoder_1_add_a), .en(rom_1_data[59]), .clk(clock_1_out), .Q(MAR_A_q));  // open: clr
  Register #(.width(10)) MAR_B (
    .D(inst_decoder_1_add_b), .en(rom_1_data[59]), .clk(clock_1_out), .Q(MAR_B_q));  // open: clr
  Adder #(.width(4)) adder_10 (.a(4'b0001), .b(flag_q), .out(adder_10_out));  // open: cin, cout
  and and_8 (and_8_out, ldecoder_1_a11, rom_1_data[35]);
  Register #(.width(64)) register_4 (
    .D(C2_dout), .en(rom_1_data[45]), .clk(clock_1_out), .Q(register_4_q));  // open: clr
  RAM #(.addrWidth(10), .dataWidth(64)) ram_1 (
    .addr(controlled_buffer_4_out), .we(rom_1_data[41]), .clk(clock_1_out), .din(controlled_buffer_9_out));  // open: oe, dout
  Comparator #(.mode("unsigned"), .width(10)) comparator_7 (
    .a(bit_extender_1_out), .b(step_counter_q), .eq(comparator_7_eq));  // open: gt, lt
  Ldecoder ldecoder_1 (
    .first(rom_1_data[7]), .second(rom_1_data[6]), .third(rom_1_data[5]), .fourth(rom_1_data[4]),
    .a11(ldecoder_1_a11), .a12(ldecoder_1_a12), .a21(ldecoder_1_a21), .a22(ldecoder_1_a22),
    .a31(ldecoder_1_a31), .a32(ldecoder_1_a32), .a41(ldecoder_1_a41), .a42(ldecoder_1_a42),
    .a51(ldecoder_1_a51), .a52(ldecoder_1_a52), .a61(ldecoder_1_a61), .a62(ldecoder_1_a62),
    .a71(ldecoder_1_a71), .a72(ldecoder_1_a72), .a81(ldecoder_1_a81), .a82(ldecoder_1_a82));
  assign bit_extender_1_out = {{6{1'b0}}, adder_10_out};  // Bit_Extender bit_extender_1
  Register #(.width(1)) register_5 (.D(comparator_7_eq), .en(1'b1), .clk(clock_1_out), .Q(register_5_q));  // open: clr
  RAM #(.addrWidth(10), .dataWidth(64)) C3 (
    .addr(controlled_buffer_3_out), .we(rom_1_data[49]), .oe(rom_1_data[46]), .clk(clock_1_out),
    .din(core16x16_1_s3), .dout(C3_dout));
  Counter #(.max('h3ff), .width(10)) step_counter (
    .clr(register_5_q), .count(rom_1_data[37]), .clk(clock_1_out), .Q(step_counter_q));  // open: load, up, D, carry
  Register #(.width(64)) B11 (.D(ramB1_dout), .en(and_11_out), .clk(clock_1_out), .Q(B11_q), .clr(rom_1_data[8]));
  Register #(.width(64)) B21 (.D(ramB1_dout), .en(ldecoder_2_a21), .clk(clock_1_out), .Q(B21_q), .clr(rom_1_data[8]));
  Register #(.width(64)) B31 (.D(ramB1_dout), .en(ldecoder_2_a31), .clk(clock_1_out), .Q(B31_q), .clr(rom_1_data[8]));
  Register #(.width(64)) B41 (.D(ramB1_dout), .en(ldecoder_2_a41), .clk(clock_1_out), .Q(B41_q), .clr(rom_1_data[8]));
  Register #(.width(64)) B51 (.D(ramB1_dout), .en(ldecoder_2_a51), .clk(clock_1_out), .Q(B51_q), .clr(rom_1_data[8]));
  Register #(.width(64)) B61 (.D(ramB1_dout), .en(ldecoder_2_a61), .clk(clock_1_out), .Q(B61_q), .clr(rom_1_data[8]));
  Register #(.width(64)) B71 (.D(ramB1_dout), .en(ldecoder_2_a71), .clk(clock_1_out), .Q(B71_q), .clr(rom_1_data[8]));
  Register #(.width(64)) B81 (.D(ramB1_dout), .en(ldecoder_2_a81), .clk(clock_1_out), .Q(B81_q), .clr(rom_1_data[8]));
  Register #(.width(64)) register_6 (
    .D(C3_dout), .en(rom_1_data[45]), .clk(clock_1_out), .Q(register_6_q));  // open: clr
  Multiplier #(.width(10)) multiplier_6 (
    .a(adder_14_out), .b(step_counter_q), .out(multiplier_6_out));  // open: cin, cout
  RAM #(.addrWidth(10), .dataWidth(64)) C4 (
    .addr(controlled_buffer_3_out), .we(rom_1_data[49]), .oe(rom_1_data[46]), .clk(clock_1_out),
    .din(core16x16_1_s4), .dout(C4_dout));
  Adder #(.width(10)) adder_11 (.a(MAR_B_q), .b(multiplier_7_out), .out(adder_11_out));  // open: cin, cout
  Register #(.width(64)) B12 (.D(ramB2_dout), .en(and_11_out), .clk(clock_1_out), .Q(B12_q), .clr(rom_1_data[8]));
  Register #(.width(64)) B22 (.D(ramB2_dout), .en(ldecoder_2_a21), .clk(clock_1_out), .Q(B22_q), .clr(rom_1_data[8]));
  Register #(.width(64)) B32 (.D(ramB2_dout), .en(ldecoder_2_a31), .clk(clock_1_out), .Q(B32_q), .clr(rom_1_data[8]));
  core16x16 core16x16_1 (
    .C11(A11_q), .C12(A12_q), .C13(A13_q), .C14(A14_q), .R11(B11_q), .R12(B12_q), .R13(B13_q), .R14(B14_q),
    .C21(A21_q), .C22(A22_q), .C23(A23_q), .C24(A24_q), .R21(B21_q), .R22(B22_q), .R23(B23_q), .R24(B24_q),
    .C31(A31_q), .C32(A32_q), .C33(A33_q), .C34(A34_q), .R31(B31_q), .R32(B32_q), .R33(B33_q), .R34(B34_q),
    .C41(A41_q), .C42(A42_q), .C43(A43_q), .C44(A44_q), .R41(B41_q), .R42(B42_q), .R43(B43_q), .R44(B44_q),
    .c51(A51_q), .c52(A52_q), .c53(A53_q), .c54(A54_q), .r51(B51_q), .r52(B52_q), .r53(B53_q), .r54(B54_q),
    .c61(A61_q), .c62(A62_q), .c63(A63_q), .c64(A64_q), .r61(B61_q), .r62(B62_q), .r63(B63_q), .r64(B64_q),
    .c71(A71_q), .c72(A72_q), .c73(A73_q), .c74(A74_q), .r71(B71_q), .r72(B72_q), .r73(B73_q), .r74(B74_q),
    .c81(A81_q), .c82(A82_q), .c83(A83_q), .c84(A84_q), .r81(B81_q), .r82(B82_q), .r83(B83_q), .r84(B84_q),
    .s1(core16x16_1_s1), .s2(core16x16_1_s2), .s3(core16x16_1_s3), .s4(core16x16_1_s4));
  Adder #(.width(10)) adder_12 (.a(adder_11_out), .b(multiplier_6_out), .out(adder_12_out));  // open: cin, cout
  Register #(.width(64)) B42 (.D(ramB2_dout), .en(ldecoder_2_a41), .clk(clock_1_out), .Q(B42_q), .clr(rom_1_data[8]));
  Register #(.width(64)) B52 (.D(ramB2_dout), .en(ldecoder_2_a51), .clk(clock_1_out), .Q(B52_q), .clr(rom_1_data[8]));
  Register #(.width(64)) B62 (.D(ramB2_dout), .en(ldecoder_2_a61), .clk(clock_1_out), .Q(B62_q), .clr(rom_1_data[8]));
  Register #(.width(64)) B72 (.D(ramB2_dout), .en(ldecoder_2_a71), .clk(clock_1_out), .Q(B72_q), .clr(rom_1_data[8]));
  Register #(.width(64)) B82 (.D(ramB2_dout), .en(ldecoder_2_a81), .clk(clock_1_out), .Q(B82_q), .clr(rom_1_data[8]));
  Register #(.width(10)) outerDimA (.D(MAR_A_q), .en(rom_1_data[58]), .clk(clock_1_out), .Q(outerDimA_q));  // open: clr
  Register #(.width(10)) outerDimB (.D(MAR_B_q), .en(rom_1_data[58]), .clk(clock_1_out), .Q(outerDimB_q));  // open: clr
  RAM #(.addrWidth(10), .dataWidth(64), .\type ("nonvolatile")) ramB1 (
    .addr(adder_12_out), .oe(and_9_out), .clk(clock_1_out), .dout(ramB1_dout));  // open: we, din
  Register #(.width(64)) register_7 (
    .D(C4_dout), .en(rom_1_data[45]), .clk(clock_1_out), .Q(register_7_q));  // open: clr
  Adder #(.width(10)) adder_13 (.a(outerDimA_q), .b(10'h1), .out(adder_13_out));  // open: cin, cout
  Adder #(.width(10)) adder_14 (.a(outerDimB_q), .b(10'h1), .out(adder_14_out));  // open: cin, cout
  Register #(.width(64)) B13 (.D(ramB1_dout), .en(ldecoder_2_a12), .clk(clock_1_out), .Q(B13_q), .clr(rom_1_data[8]));
  Divider #(.width(10)) divider_2 (.a(adder_14_out), .b(10'h2), .out(divider_2_out));  // open: upper, rem
  Register #(.width(64)) B23 (.D(ramB1_dout), .en(ldecoder_2_a22), .clk(clock_1_out), .Q(B23_q), .clr(rom_1_data[8]));
  Register #(.width(64)) B33 (.D(ramB1_dout), .en(ldecoder_2_a32), .clk(clock_1_out), .Q(B33_q), .clr(rom_1_data[8]));
  Register #(.width(64)) B43 (.D(ramB1_dout), .en(ldecoder_2_a42), .clk(clock_1_out), .Q(B43_q), .clr(rom_1_data[8]));
  Register #(.width(64)) B53 (.D(ramB1_dout), .en(ldecoder_2_a52), .clk(clock_1_out), .Q(B53_q), .clr(rom_1_data[8]));
  Register #(.width(64)) B63 (.D(ramB1_dout), .en(ldecoder_2_a62), .clk(clock_1_out), .Q(B63_q), .clr(rom_1_data[8]));
  Register #(.width(64)) B73 (.D(ramB1_dout), .en(ldecoder_2_a72), .clk(clock_1_out), .Q(B73_q), .clr(rom_1_data[8]));
  Register #(.width(64)) B83 (.D(ramB1_dout), .en(ldecoder_2_a82), .clk(clock_1_out), .Q(B83_q), .clr(rom_1_data[8]));
  Clock clock_1 (.out(clock_1_out));
  Divider #(.width(10)) divider_3 (.a(adder_13_out), .b(10'h2), .out(divider_3_out));  // open: upper, rem
  Counter #(.max('hffff), .width(16)) clock_cycle_counter (
    .up(rom_1_data[63]), .count(rom_1_data[63]), .clk(clock_1_out), .Q(clock_cycle_counter_q));  // open: clr, load, D, carry
  Adder #(.width(10)) adder_15 (.a(10'h1), .b(adder_12_out), .out(adder_15_out));  // open: cin, cout
  RAM #(.addrWidth(10), .dataWidth(64), .\type ("nonvolatile")) ramB2 (
    .addr(adder_15_out), .oe(and_9_out), .clk(clock_1_out), .dout(ramB2_dout));  // open: we, din
  Register #(.width(64)) B14 (.D(ramB2_dout), .en(ldecoder_2_a12), .clk(clock_1_out), .Q(B14_q), .clr(rom_1_data[8]));
  Register #(.width(64)) B24 (.D(ramB2_dout), .en(ldecoder_2_a22), .clk(clock_1_out), .Q(B24_q), .clr(rom_1_data[8]));
  Register #(.width(64)) B34 (.D(ramB2_dout), .en(ldecoder_2_a32), .clk(clock_1_out), .Q(B34_q), .clr(rom_1_data[8]));
  Register #(.width(64)) B44 (.D(ramB2_dout), .en(ldecoder_2_a42), .clk(clock_1_out), .Q(B44_q), .clr(rom_1_data[8]));
  Register #(.width(64)) B54 (.D(ramB2_dout), .en(ldecoder_2_a52), .clk(clock_1_out), .Q(B54_q), .clr(rom_1_data[8]));
  Register #(.width(64)) B64 (.D(ramB2_dout), .en(ldecoder_2_a62), .clk(clock_1_out), .Q(B64_q), .clr(rom_1_data[8]));
  Register #(.width(64)) B74 (.D(ramB2_dout), .en(ldecoder_2_a72), .clk(clock_1_out), .Q(B74_q), .clr(rom_1_data[8]));
  Register #(.width(64)) B84 (.D(ramB2_dout), .en(ldecoder_2_a82), .clk(clock_1_out), .Q(B84_q), .clr(rom_1_data[8]));
  and and_9 (and_9_out, rom_1_data[53], not_5_out);
  not not_5 (not_5_out, comparator_7_eq);
  and and_10 (and_10_out, comparator_7_eq, rom_1_data[36]);
  Register #(.width(1)) register_8 (.D(comparator_8_eq), .en(1'b1), .clk(clock_1_out), .Q(register_8_q));  // open: clr
  Counter #(.max('h3ff), .width(10)) column_counter (
    .clr(register_8_q), .up(comparator_7_eq), .count(and_10_out), .clk(clock_1_out), .Q(column_counter_q));  // open: load, D, carry
  ROM #(.addrWidth(12), .dataWidth(64)) rom_1 (
    .addr(counter_2_q), .data({rom_1_data[63:49], rom_1_data_2[0], rom_1_data_2[1], rom_1_data[46:0]}));
  and and_11 (and_11_out, ldecoder_2_a11, rom_1_data[35]);
  Ldecoder ldecoder_2 (
    .first(rom_1_data[3]), .second(rom_1_data[2]), .third(rom_1_data[1]), .fourth(rom_1_data[0]),
    .a11(ldecoder_2_a11), .a12(ldecoder_2_a12), .a21(ldecoder_2_a21), .a22(ldecoder_2_a22),
    .a31(ldecoder_2_a31), .a32(ldecoder_2_a32), .a41(ldecoder_2_a41), .a42(ldecoder_2_a42),
    .a51(ldecoder_2_a51), .a52(ldecoder_2_a52), .a61(ldecoder_2_a61), .a62(ldecoder_2_a62),
    .a71(ldecoder_2_a71), .a72(ldecoder_2_a72), .a81(ldecoder_2_a81), .a82(ldecoder_2_a82));
  Comparator #(.mode("unsigned"), .width(10)) comparator_8 (
    .a(divider_2_out), .b(column_counter_q), .eq(comparator_8_eq));  // open: gt, lt
  Multiplier #(.width(10)) multiplier_7 (.a(10'h2), .b(column_counter_q), .out(multiplier_7_out));  // open: cin, cout
  Register #(.width(1)) register_9 (.D(rom_1_data[40]), .en(1'b1), .clk(clock_1_out), .Q(register_9_q));  // open: clr
  Register #(.width(1)) register_10 (.D(and_7_out), .en(1'b1), .clk(clock_1_out), .Q(register_10_q));  // open: clr
  Counter #(.max('h7), .width(3)) counter_1 (
    .count(register_10_q), .clk(clock_1_out), .Q(counter_1_q));  // open: clr, load, up, D, carry
  Register #(.width(1)) register_11 (
    .D(rom_1_data[38]), .en(rom_1_data[38]), .clk(clock_1_out), .Q(register_11_q));  // open: clr
  Comparator #(.width(4)) comparator_9 (.a(counter_2_q[11:8]), .b(4'b0100), .eq(comparator_9_eq));  // open: gt, lt
  Comparator #(.width(4)) comparator_10 (.a(counter_2_q[11:8]), .b(4'b0011), .eq(comparator_10_eq));  // open: gt, lt
  not not_6 (not_6_out, register_11_q);
  Decoder #(.select(3)) decoder_3 (
    .out0(decoder_3_out0), .out1(decoder_3_out1), .out2(decoder_3_out2), .out3(decoder_3_out3),
    .sel(counter_1_q));  // open: out4, out5, out6, out7, en
  and and_12 (and_12_out, and_5_out, comparator_9_eq);
  and and_13 (and_13_out, comparator_10_eq, comparator_7_eq);
  or or_3 (or_3_out, register_12_q, and_13_out, register_9_q);
  Counter #(.trigger("falling")) counter_2 (
    .clr(or_3_out), .up(and_14_out), .count(and_14_out), .clk(clock_1_out), .Q(counter_2_q[7:0]));  // open: load, D, carry
  and and_14 (and_14_out, not_6_out, rom_1_data[62]);
  Comparator #(.width(4)) comparator_11 (.a(counter_2_q[11:8]), .b(4'b0010), .eq(comparator_11_eq));  // open: gt, lt
  not not_7 (not_7_out, and_7_out);
  Register #(.width(1)) register_12 (.D(and_12_out), .en(1'b1), .Q(register_12_q));  // open: clk, clr
  xor xor_1 (xor_1_out, not_7_out, register_10_q);
  and and_15 (and_15_out, xor_1_out, decoder_3_out0);
  and and_16 (and_16_out, decoder_3_out1, xor_1_out);
  and and_17 (and_17_out, xor_1_out, decoder_3_out2);
  and and_18 (and_18_out, xor_1_out, decoder_3_out3);
  Register #(.width(1)) register_13 (.D(register_10_q), .en(1'b1), .clk(clock_1_out), .Q(register_13_q));  // open: clr
  Counter #(.max('hffff), .width(16)) counter_3 (
    .clr(register_13_q), .count(comparator_11_eq), .clk(clock_1_out), .Q(counter_3_q));  // open: load, up, D, carry
  Register #(.width(16)) register_14 (
    .D(counter_3_q), .en(and_15_out), .clk(clock_1_out), .Q(register_14_q));  // open: clr
  Register #(.width(16)) register_15 (
    .D(counter_3_q), .en(and_16_out), .clk(clock_1_out), .Q(register_15_q));  // open: clr
  Register #(.width(16)) register_16 (
    .D(counter_3_q), .en(and_17_out), .clk(clock_1_out), .Q(register_16_q));  // open: clr
  Register #(.width(16)) register_17 (
    .D(counter_3_q), .en(and_18_out), .clk(clock_1_out), .Q(register_17_q));  // open: clr
  Hex_Digit_Display hex_digit_display_1 (.value(register_14_q[15:12]));  // open: dp
  Hex_Digit_Display hex_digit_display_2 (.value(register_14_q[11:8]));  // open: dp
  Hex_Digit_Display hex_digit_display_3 (.value(register_15_q[15:12]));  // open: dp
  Hex_Digit_Display hex_digit_display_4 (.value(register_15_q[11:8]));  // open: dp
  Hex_Digit_Display hex_digit_display_5 (.value(register_16_q[15:12]));  // open: dp
  Hex_Digit_Display hex_digit_display_6 (.value(register_16_q[11:8]));  // open: dp
  Hex_Digit_Display hex_digit_display_7 (.value(register_17_q[15:12]));  // open: dp
  Hex_Digit_Display hex_digit_display_8 (.value(register_17_q[11:8]));  // open: dp
  Hex_Digit_Display hex_digit_display_9 (.value(register_14_q[7:4]));  // open: dp
  Hex_Digit_Display hex_digit_display_10 (.value(register_14_q[3:0]));  // open: dp
  Hex_Digit_Display hex_digit_display_11 (.value(register_15_q[7:4]));  // open: dp
  Hex_Digit_Display hex_digit_display_12 (.value(register_15_q[3:0]));  // open: dp
  Hex_Digit_Display hex_digit_display_13 (.value(register_16_q[7:4]));  // open: dp
  Hex_Digit_Display hex_digit_display_14 (.value(register_16_q[3:0]));  // open: dp
  Hex_Digit_Display hex_digit_display_15 (.value(register_17_q[7:4]));  // open: dp
  Hex_Digit_Display hex_digit_display_16 (.value(register_17_q[3:0]));  // open: dp
  Counter #(.max('hffff), .width(16)) counter_4 (
    .clr(register_13_q), .count(comparator_9_eq), .clk(clock_1_out), .Q(counter_4_q));  // open: load, up, D, carry
  Register #(.width(16)) register_18 (
    .D(counter_4_q), .en(and_15_out), .clk(clock_1_out), .Q(register_18_q));  // open: clr
  Register #(.width(16)) register_19 (
    .D(counter_4_q), .en(and_16_out), .clk(clock_1_out), .Q(register_19_q));  // open: clr
  Register #(.width(16)) register_20 (
    .D(counter_4_q), .en(and_17_out), .clk(clock_1_out), .Q(register_20_q));  // open: clr
  Register #(.width(16)) register_21 (
    .D(counter_4_q), .en(and_18_out), .clk(clock_1_out), .Q(register_21_q));  // open: clr
  Hex_Digit_Display hex_digit_display_17 (.value(register_18_q[15:12]));  // open: dp
  Hex_Digit_Display hex_digit_display_18 (.value(register_19_q[15:12]));  // open: dp
  Hex_Digit_Display hex_digit_display_19 (.value(register_20_q[15:12]));  // open: dp
  Hex_Digit_Display hex_digit_display_20 (.value(register_21_q[15:12]));  // open: dp
  Hex_Digit_Display hex_digit_display_21 (.value(register_18_q[11:8]));  // open: dp
  Hex_Digit_Display hex_digit_display_22 (.value(register_18_q[7:4]));  // open: dp
  Hex_Digit_Display hex_digit_display_23 (.value(register_19_q[11:8]));  // open: dp
  Hex_Digit_Display hex_digit_display_24 (.value(register_19_q[7:4]));  // open: dp
  Hex_Digit_Display hex_digit_display_25 (.value(register_20_q[11:8]));  // open: dp
  Hex_Digit_Display hex_digit_display_26 (.value(register_20_q[7:4]));  // open: dp
  Hex_Digit_Display hex_digit_display_27 (.value(register_21_q[11:8]));  // open: dp
  Hex_Digit_Display hex_digit_display_28 (.value(register_21_q[7:4]));  // open: dp
  Hex_Digit_Display hex_digit_display_29 (.value(clock_cycle_counter_q[15:12]));  // open: dp
  Hex_Digit_Display hex_digit_display_30 (.value(register_18_q[3:0]));  // open: dp
  Hex_Digit_Display hex_digit_display_31 (.value(register_19_q[3:0]));  // open: dp
  Hex_Digit_Display hex_digit_display_32 (.value(register_20_q[3:0]));  // open: dp
  Hex_Digit_Display hex_digit_display_33 (.value(register_21_q[3:0]));  // open: dp
  Hex_Digit_Display hex_digit_display_34 (.value(clock_cycle_counter_q[11:8]));  // open: dp
  Hex_Digit_Display hex_digit_display_35 (.value(clock_cycle_counter_q[7:4]));  // open: dp
  Hex_Digit_Display hex_digit_display_36 (.value(clock_cycle_counter_q[3:0]));  // open: dp
  Counter #(.max('hffff), .width(16)) counter_5 (
    .clr(register_13_q), .count(comparator_10_eq), .clk(clock_1_out), .Q(counter_5_q));  // open: load, up, D, carry
  Register #(.width(16)) register_22 (
    .D(counter_5_q), .en(and_15_out), .clk(clock_1_out), .Q(register_22_q));  // open: clr
  Register #(.width(16)) register_23 (
    .D(counter_5_q), .en(and_16_out), .clk(clock_1_out), .Q(register_23_q));  // open: clr
  Register #(.width(16)) register_24 (
    .D(counter_5_q), .en(and_17_out), .clk(clock_1_out), .Q(register_24_q));  // open: clr
  Register #(.width(16)) register_25 (
    .D(counter_5_q), .en(and_18_out), .clk(clock_1_out), .Q(register_25_q));  // open: clr
  Hex_Digit_Display hex_digit_display_37 (.value(register_22_q[15:12]));  // open: dp
  Hex_Digit_Display hex_digit_display_38 (.value(register_22_q[11:8]));  // open: dp
  Hex_Digit_Display hex_digit_display_39 (.value(register_23_q[15:12]));  // open: dp
  Hex_Digit_Display hex_digit_display_40 (.value(register_23_q[11:8]));  // open: dp
  Hex_Digit_Display hex_digit_display_41 (.value(register_24_q[15:12]));  // open: dp
  Hex_Digit_Display hex_digit_display_42 (.value(register_24_q[11:8]));  // open: dp
  Hex_Digit_Display hex_digit_display_43 (.value(register_25_q[15:12]));  // open: dp
  Hex_Digit_Display hex_digit_display_44 (.value(register_25_q[11:8]));  // open: dp
  Hex_Digit_Display hex_digit_display_45 (.value(register_22_q[7:4]));  // open: dp
  Hex_Digit_Display hex_digit_display_46 (.value(register_22_q[3:0]));  // open: dp
  Hex_Digit_Display hex_digit_display_47 (.value(register_23_q[7:4]));  // open: dp
  Hex_Digit_Display hex_digit_display_48 (.value(register_23_q[3:0]));  // open: dp
  Hex_Digit_Display hex_digit_display_49 (.value(register_24_q[7:4]));  // open: dp
  Hex_Digit_Display hex_digit_display_50 (.value(register_24_q[3:0]));  // open: dp
  Hex_Digit_Display hex_digit_display_51 (.value(register_25_q[7:4]));  // open: dp
  Hex_Digit_Display hex_digit_display_52 (.value(register_25_q[3:0]));  // open: dp

  // Notes on the sheet:
  //   row/2
  //   column
  //   base_address
  //   RAM_Inst
  //   c1_address
  //   c2_address
  //   c3_address
  //   c4_address
  //   A1
  //   RAM_C1
  //   A2
  //   RAM_C2
  //   inner_dim
  //   Final_Output_RAM
  //   RAM_C3
  //   RAM_C4
  //   B1
  //   B2
  //   contents of rom_1 (hex, n*v repeats v):
  //   d000000000000100 d000008000000000 c000008000000000 c800010000000000 252*0 e400000000000000
  //   d000000000000000 d000000000000000 c800008000000000 c800010000000000 251*0 e064002000000000
  //   d064003800000000 d064003000000088 c06400b000000044 c0640030000000cc c064003000000022
  //   c0640030000000aa c064003000000066 c0640030000000ee c064003000000011 c064003000000099
  //   c064003000000055 c0640030000000dd c064003000000033 c0640030000000bb c064003000000077
  //   c0640030000000ff c064003000000000 238*0 e006100000000000 d000000000000000 d000008000000000
  //   c000008000000000 c800010000000000 251*0 c000400000000000 d000200000000000 d000020000000000
  //   c001028000000000 c800820000000000 c001820000000000 c000000000000000 c000010000000000 760*0
  //   e200000000000000 d000000000000000 d000000000000000 c000008000000000 c800010000000000 251*0
  //   4000000000
  //   0. fourth bit
  //   1. third bit
  //   2. second bit
  //   3. first bit
  //   4. fourth bit
  //   5. third bit
  //   6. second bit
  //   7. first bit
  //   8. registers reset
  //   35. 1st load WE
  //   37. step counter g5
  //   38. rom stop
  //   39. inst_mbr we
  //   50. row counter g5
  //   53. Ram b1,b2 oe
  //   54. ram a1,a2 oe
  //   57. pc load
  //   58. dim we (flag+reg)
  //   61. pc g5
  //   62. rom counter g5
  //   Program Control Lines Label
  //   Bdecoder
  //   Adecoder
  //   36. column counter g5
  //   40. rom counter reset
  //   41. final output ram we
  //   44. execution counter g5
  //   45. output registers we
  //   47. output decoder first bit
  //   48. output decoder 0th bit
  //   46. suboutput ram first oe
  //   49. suboutput rams we
  //   59. mar a,b, opcode we
  //   60. inst_ram oe & mar_inst we
  //   63. clock cycles counter g5
  //   BLOCK LOAD CYCLES
  //   BLOCK STORE CYCLES
  //   Total Number of Cycles
  //   EXECUTE CYCLES
endmodule

module adderCore2x2 (
  input  c1in,
  input  [63:0] A1,
  input  [63:0] B1,
  input  c2in,
  input  [63:0] A2,
  input  [63:0] B2,
  input  c3in,
  input  [63:0] A3,
  input  [63:0] B3,
  input  c4in,
  input  [63:0] A4,
  input  [63:0] B4,
  output [63:0] S1,
  output [63:0] S2,
  output [63:0] S3,
  output [63:0] S4
);

  Adder #(.width(64)) adder_1 (.a(A1), .b(B1), .out(S1), .cin(c1in));  // open: cout
  Adder #(.width(64)) adder_2 (.a(A2), .b(B2), .out(S2), .cin(c2in));  // open: cout
  Adder #(.width(64)) adder_3 (.a(A3), .b(B3), .out(S3), .cin(c3in));  // open: cout
  Adder #(.width(64)) adder_4 (.a(A4), .b(B4), .out(S4), .cin(c4in));  // open: cout
endmodule

module core2x2 (
  input  [63:0] A1,
  input  [63:0] A2,
  input  [63:0] A3,
  input  [63:0] A4,
  input  [63:0] B1,
  input  [63:0] B2,
  input  [63:0] B3,
  input  [63:0] B4,
  output [63:0] C1,
  output [63:0] C2,
  output [63:0] C3,
  output [63:0] C4
);

  wire [63:0] multiplier_1_out, multiplier_2_out, multiplier_3_out, multiplier_4_out, multiplier_5_out,
       multiplier_6_out, multiplier_7_out, multiplier_8_out;

  Multiplier #(.width(64)) multiplier_1 (.a(A1), .b(B1), .out(multiplier_1_out));  // open: cin, cout
  Multiplier #(.width(64)) multiplier_2 (.a(A2), .b(B3), .out(multiplier_2_out));  // open: cin, cout
  Multiplier #(.width(64)) multiplier_3 (.a(A1), .b(B2), .out(multiplier_3_out));  // open: cin, cout
  Multiplier #(.width(64)) multiplier_4 (.a(A2), .b(B4), .out(multiplier_4_out));  // open: cin, cout
  Multiplier #(.width(64)) multiplier_5 (.a(A3), .b(B1), .out(multiplier_5_out));  // open: cin, cout
  Multiplier #(.width(64)) multiplier_6 (.a(A4), .b(B3), .out(multiplier_6_out));  // open: cin, cout
  Multiplier #(.width(64)) multiplier_7 (.a(A3), .b(B2), .out(multiplier_7_out));  // open: cin, cout
  Multiplier #(.width(64)) multiplier_8 (.a(A4), .b(B4), .out(multiplier_8_out));  // open: cin, cout
  Adder #(.width(64)) adder_1 (.a(multiplier_1_out), .b(multiplier_2_out), .out(C1));  // open: cin, cout
  Adder #(.width(64)) adder_2 (.a(multiplier_3_out), .b(multiplier_4_out), .out(C2));  // open: cin, cout
  Adder #(.width(64)) adder_3 (.a(multiplier_5_out), .b(multiplier_6_out), .out(C3));  // open: cin, cout
  Adder #(.width(64)) adder_4 (.a(multiplier_7_out), .b(multiplier_8_out), .out(C4));  // open: cin, cout
endmodule

module core16x16 (
  input  [63:0] C11,
  input  [63:0] C12,
  input  [63:0] C13,
  input  [63:0] C14,
  input  [63:0] R11,
  input  [63:0] R12,
  input  [63:0] R13,
  input  [63:0] R14,
  input  [63:0] C21,
  input  [63:0] C22,
  input  [63:0] C23,
  input  [63:0] C24,
  input  [63:0] R21,
  input  [63:0] R22,
  input  [63:0] R23,
  input  [63:0] R24,
  input  [63:0] C31,
  input  [63:0] C32,
  input  [63:0] C33,
  input  [63:0] C34,
  input  [63:0] R31,
  input  [63:0] R32,
  input  [63:0] R33,
  input  [63:0] R34,
  input  [63:0] C41,
  input  [63:0] C42,
  input  [63:0] C43,
  input  [63:0] C44,
  input  [63:0] R41,
  input  [63:0] R42,
  input  [63:0] R43,
  input  [63:0] R44,
  input  [63:0] c51,
  input  [63:0] c52,
  input  [63:0] c53,
  input  [63:0] c54,
  input  [63:0] r51,
  input  [63:0] r52,
  input  [63:0] r53,
  input  [63:0] r54,
  input  [63:0] c61,
  input  [63:0] c62,
  input  [63:0] c63,
  input  [63:0] c64,
  input  [63:0] r61,
  input  [63:0] r62,
  input  [63:0] r63,
  input  [63:0] r64,
  input  [63:0] c71,
  input  [63:0] c72,
  input  [63:0] c73,
  input  [63:0] c74,
  input  [63:0] r71,
  input  [63:0] r72,
  input  [63:0] r73,
  input  [63:0] r74,
  input  [63:0] c81,
  input  [63:0] c82,
  input  [63:0] c83,
  input  [63:0] c84,
  input  [63:0] r81,
  input  [63:0] r82,
  input  [63:0] r83,
  input  [63:0] r84,
  output [63:0] s1,
  output [63:0] s2,
  output [63:0] s3,
  output [63:0] s4
);

  wire [63:0] addercore2x2_1_s1, addercore2x2_1_s2, addercore2x2_1_s3, addercore2x2_1_s4, addercore2x2_2_s1,
       addercore2x2_2_s2, addercore2x2_2_s3, addercore2x2_2_s4, addercore2x2_3_s1, addercore2x2_3_s2,
       addercore2x2_3_s3, addercore2x2_3_s4, addercore2x2_4_s1, addercore2x2_4_s2, addercore2x2_4_s3,
       addercore2x2_4_s4, addercore2x2_5_s1, addercore2x2_5_s2, addercore2x2_5_s3, addercore2x2_5_s4,
       addercore2x2_6_s1, addercore2x2_6_s2, addercore2x2_6_s3, addercore2x2_6_s4, core2x2_1_c1,
       core2x2_1_c2, core2x2_1_c3, core2x2_1_c4, core2x2_2_c1, core2x2_2_c2, core2x2_2_c3, core2x2_2_c4,
       core2x2_3_c1, core2x2_3_c2, core2x2_3_c3, core2x2_3_c4, core2x2_4_c1, core2x2_4_c2, core2x2_4_c3,
       core2x2_4_c4, core2x2_5_c1, core2x2_5_c2, core2x2_5_c3, core2x2_5_c4, core2x2_6_c1, core2x2_6_c2,
       core2x2_6_c3, core2x2_6_c4, core2x2_7_c1, core2x2_7_c2, core2x2_7_c3, core2x2_7_c4, core2x2_8_c1,
       core2x2_8_c2, core2x2_8_c3, core2x2_8_c4;

  core2x2 core2x2_1 (
    .A1(C11), .A2(C12), .A3(C13), .A4(C14), .B1(R11), .B2(R12), .B3(R13), .B4(R14), .C1(core2x2_1_c1),
    .C2(core2x2_1_c2), .C3(core2x2_1_c3), .C4(core2x2_1_c4));
  core2x2 core2x2_2 (
    .A1(C21), .A2(C22), .A3(C23), .A4(C24), .B1(R21), .B2(R22), .B3(R23), .B4(R24), .C1(core2x2_2_c1),
    .C2(core2x2_2_c2), .C3(core2x2_2_c3), .C4(core2x2_2_c4));
  core2x2 core2x2_3 (
    .A1(C31), .A2(C32), .A3(C33), .A4(C34), .B1(R31), .B2(R32), .B3(R33), .B4(R34), .C1(core2x2_3_c1),
    .C2(core2x2_3_c2), .C3(core2x2_3_c3), .C4(core2x2_3_c4));
  core2x2 core2x2_4 (
    .A1(C41), .A2(C42), .A3(C43), .A4(C44), .B1(R41), .B2(R42), .B3(R43), .B4(R44), .C1(core2x2_4_c1),
    .C2(core2x2_4_c2), .C3(core2x2_4_c3), .C4(core2x2_4_c4));
  core2x2 core2x2_5 (
    .A1(c51), .A2(c52), .A3(c53), .A4(c54), .B1(r51), .B2(r52), .B3(r53), .B4(r54), .C1(core2x2_5_c1),
    .C2(core2x2_5_c2), .C3(core2x2_5_c3), .C4(core2x2_5_c4));
  core2x2 core2x2_6 (
    .A1(c61), .A2(c62), .A3(c63), .A4(c64), .B1(r61), .B2(r62), .B3(r63), .B4(r64), .C1(core2x2_6_c1),
    .C2(core2x2_6_c2), .C3(core2x2_6_c3), .C4(core2x2_6_c4));
  core2x2 core2x2_7 (
    .A1(c71), .A2(c72), .A3(c73), .A4(c74), .B1(r71), .B2(r72), .B3(r73), .B4(r74), .C1(core2x2_7_c1),
    .C2(core2x2_7_c2), .C3(core2x2_7_c3), .C4(core2x2_7_c4));
  core2x2 core2x2_8 (
    .A1(c81), .A2(c82), .A3(c83), .A4(c84), .B1(r81), .B2(r82), .B3(r83), .B4(r84), .C1(core2x2_8_c1),
    .C2(core2x2_8_c2), .C3(core2x2_8_c3), .C4(core2x2_8_c4));
  adderCore2x2 addercore2x2_1 (
    .A1(core2x2_1_c1), .B1(core2x2_2_c1), .A2(core2x2_1_c2), .B2(core2x2_2_c2), .A3(core2x2_1_c3),
    .B3(core2x2_2_c3), .A4(core2x2_1_c4), .B4(core2x2_2_c4), .S1(addercore2x2_1_s1), .S2(addercore2x2_1_s2),
    .S3(addercore2x2_1_s3), .S4(addercore2x2_1_s4));  // open: c1in, c2in, c3in, c4in
  adderCore2x2 addercore2x2_2 (
    .A1(addercore2x2_1_s1), .B1(core2x2_3_c1), .A2(addercore2x2_1_s2), .B2(core2x2_3_c2),
    .A3(addercore2x2_1_s3), .B3(core2x2_3_c3), .A4(addercore2x2_1_s4), .B4(core2x2_3_c4),
    .S1(addercore2x2_2_s1), .S2(addercore2x2_2_s2), .S3(addercore2x2_2_s3), .S4(addercore2x2_2_s4));  // open: c1in, c2in, c3in, c4in
  adderCore2x2 addercore2x2_3 (
    .A1(addercore2x2_2_s1), .B1(core2x2_4_c1), .A2(addercore2x2_2_s2), .B2(core2x2_4_c2),
    .A3(addercore2x2_2_s3), .B3(core2x2_4_c3), .A4(addercore2x2_2_s4), .B4(core2x2_4_c4),
    .S1(addercore2x2_3_s1), .S2(addercore2x2_3_s2), .S3(addercore2x2_3_s3), .S4(addercore2x2_3_s4));  // open: c1in, c2in, c3in, c4in
  adderCore2x2 addercore2x2_4 (
    .A1(addercore2x2_3_s1), .B1(core2x2_5_c1), .A2(addercore2x2_3_s2), .B2(core2x2_5_c2),
    .A3(addercore2x2_3_s3), .B3(core2x2_5_c3), .A4(addercore2x2_3_s4), .B4(core2x2_5_c4),
    .S1(addercore2x2_4_s1), .S2(addercore2x2_4_s2), .S3(addercore2x2_4_s3), .S4(addercore2x2_4_s4));  // open: c1in, c2in, c3in, c4in
  adderCore2x2 addercore2x2_5 (
    .A1(addercore2x2_4_s1), .B1(core2x2_6_c1), .A2(addercore2x2_4_s2), .B2(core2x2_6_c2),
    .A3(addercore2x2_4_s3), .B3(core2x2_6_c3), .A4(addercore2x2_4_s4), .B4(core2x2_6_c4),
    .S1(addercore2x2_5_s1), .S2(addercore2x2_5_s2), .S3(addercore2x2_5_s3), .S4(addercore2x2_5_s4));  // open: c1in, c2in, c3in, c4in
  adderCore2x2 addercore2x2_6 (
    .A1(core2x2_7_c1), .B1(addercore2x2_5_s1), .A2(core2x2_7_c2), .B2(addercore2x2_5_s2), .A3(core2x2_7_c3),
    .B3(addercore2x2_5_s3), .A4(core2x2_7_c4), .B4(addercore2x2_5_s4), .S1(addercore2x2_6_s1),
    .S2(addercore2x2_6_s2), .S3(addercore2x2_6_s3), .S4(addercore2x2_6_s4));  // open: c1in, c2in, c3in, c4in
  adderCore2x2 addercore2x2_7 (
    .A1(core2x2_8_c1), .B1(addercore2x2_6_s1), .A2(core2x2_8_c2), .B2(addercore2x2_6_s2), .A3(core2x2_8_c3),
    .B3(addercore2x2_6_s3), .A4(core2x2_8_c4), .B4(addercore2x2_6_s4), .S1(s1), .S2(s2), .S3(s3), .S4(s4));  // open: c1in, c2in, c3in, c4in
endmodule

module inst_decoder (
  input  [27:0] instruction,
  output [3:0] flag,
  output [3:0] opcode,
  output [9:0] add_A,
  output [9:0] add_B
);

  wire undriven, undriven_2, undriven_3, undriven_4, undriven_5, undriven_6, undriven_7, undriven_8,
       undriven_9, undriven_10, undriven_11, undriven_12, undriven_13, undriven_14, undriven_15, undriven_16,
       undriven_17, undriven_18, undriven_19, undriven_20, undriven_21;
  wire [15:0] counter_1_q, register_1_q, register_2_q, register_3_q, register_4_q, register_5_q,
       register_6_q, register_7_q, register_8_q;

  Counter #(.max('hffff), .width(16)) counter_1 (
    .clr(undriven_3), .count(undriven), .clk(undriven_2), .Q(counter_1_q));  // open: load, up, D, carry
  Counter #(.max('hffff), .width(16)) counter_2 (
    .clr(undriven_4), .count(undriven_2), .clk(undriven_5), .Q(counter_1_q));  // open: load, up, D, carry
  Register #(.width(16)) register_1 (
    .D(counter_1_q), .en(undriven_6), .clk(undriven_14), .Q(register_1_q));  // open: clr
  Register #(.width(16)) register_2 (
    .D(counter_1_q), .en(undriven_8), .clk(undriven_16), .Q(register_2_q));  // open: clr
  Register #(.width(16)) register_3 (
    .D(counter_1_q), .en(undriven_9), .clk(undriven_17), .Q(register_3_q));  // open: clr
  Register #(.width(16)) register_4 (
    .D(counter_1_q), .en(undriven_12), .clk(undriven_20), .Q(register_4_q));  // open: clr
  Register #(.width(16)) register_5 (
    .D(counter_1_q), .en(undriven_7), .clk(undriven_15), .Q(register_5_q));  // open: clr
  Register #(.width(16)) register_6 (
    .D(counter_1_q), .en(undriven_10), .clk(undriven_18), .Q(register_6_q));  // open: clr
  Register #(.width(16)) register_7 (
    .D(counter_1_q), .en(undriven_11), .clk(undriven_19), .Q(register_7_q));  // open: clr
  Register #(.width(16)) register_8 (
    .D(counter_1_q), .en(undriven_13), .clk(undriven_21), .Q(register_8_q));  // open: clr
  Hex_Digit_Display hex_digit_display_1 (.value(register_1_q[15:12]));  // open: dp
  Hex_Digit_Display hex_digit_display_2 (.value(register_2_q[15:12]));  // open: dp
  Hex_Digit_Display hex_digit_display_3 (.value(register_3_q[15:12]));  // open: dp
  Hex_Digit_Display hex_digit_display_4 (.value(register_4_q[15:12]));  // open: dp
  Hex_Digit_Display hex_digit_display_5 (.value(register_5_q[15:12]));  // open: dp
  Hex_Digit_Display hex_digit_display_6 (.value(register_6_q[15:12]));  // open: dp
  Hex_Digit_Display hex_digit_display_7 (.value(register_7_q[15:12]));  // open: dp
  Hex_Digit_Display hex_digit_display_8 (.value(register_8_q[15:12]));  // open: dp
  Hex_Digit_Display hex_digit_display_9 (.value(register_1_q[11:8]));  // open: dp
  Hex_Digit_Display hex_digit_display_10 (.value(register_1_q[7:4]));  // open: dp
  Hex_Digit_Display hex_digit_display_11 (.value(register_2_q[11:8]));  // open: dp
  Hex_Digit_Display hex_digit_display_12 (.value(register_2_q[7:4]));  // open: dp
  Hex_Digit_Display hex_digit_display_13 (.value(register_3_q[11:8]));  // open: dp
  Hex_Digit_Display hex_digit_display_14 (.value(register_3_q[7:4]));  // open: dp
  Hex_Digit_Display hex_digit_display_15 (.value(register_4_q[11:8]));  // open: dp
  Hex_Digit_Display hex_digit_display_16 (.value(register_4_q[7:4]));  // open: dp
  Hex_Digit_Display hex_digit_display_17 (.value(register_5_q[11:8]));  // open: dp
  Hex_Digit_Display hex_digit_display_18 (.value(register_5_q[7:4]));  // open: dp
  Hex_Digit_Display hex_digit_display_19 (.value(register_6_q[11:8]));  // open: dp
  Hex_Digit_Display hex_digit_display_20 (.value(register_6_q[7:4]));  // open: dp
  Hex_Digit_Display hex_digit_display_21 (.value(register_7_q[11:8]));  // open: dp
  Hex_Digit_Display hex_digit_display_22 (.value(register_7_q[7:4]));  // open: dp
  Hex_Digit_Display hex_digit_display_23 (.value(register_8_q[11:8]));  // open: dp
  Hex_Digit_Display hex_digit_display_24 (.value(register_8_q[7:4]));  // open: dp
  Hex_Digit_Display hex_digit_display_25 (.value(register_1_q[3:0]));  // open: dp
  Hex_Digit_Display hex_digit_display_26 (.value(register_2_q[3:0]));  // open: dp
  Hex_Digit_Display hex_digit_display_27 (.value(register_3_q[3:0]));  // open: dp
  Hex_Digit_Display hex_digit_display_28 (.value(register_4_q[3:0]));  // open: dp
  Hex_Digit_Display hex_digit_display_29 (.value(register_5_q[3:0]));  // open: dp
  Hex_Digit_Display hex_digit_display_30 (.value(register_6_q[3:0]));  // open: dp
  Hex_Digit_Display hex_digit_display_31 (.value(register_7_q[3:0]));  // open: dp
  Hex_Digit_Display hex_digit_display_32 (.value(register_8_q[3:0]));  // open: dp

  assign add_A = instruction[19:10];
  assign add_B = instruction[9:0];
  assign flag = instruction[27:24];
  assign opcode = instruction[23:20];

  // Notes on the sheet:
  //   BLOCK STORE CYCLES
  //   BLOCK STORE CYCLES
endmodule

module experimenting (
  input  [7:0] in_1,
  input  in_2,
  input  [7:0] in_3,
  input  in_4,
  input  in_5,
  input  in_6,
  input  in_7,
  input  [7:0] in_8,
  input  [1:0] in_9,
  input  [7:0] in_10,
  output [7:0] out_11
);

  wire clock_1_out, counter_1_carry, decoder_1_out0, decoder_1_out1, decoder_1_out2, decoder_1_out3,
       not_1_out;
  wire [7:0] adder_1_out, adder_2_out, adder_3_out, controlled_buffer_1_out, counter_1_q, multiplier_1_out,
       ram_1_dout, ram_2_dout, register_1_q, register_2_q, register_3_q;

  Clock clock_1 (.out(clock_1_out));
  Counter #(.max('h2)) counter_1 (
    .up(1'b1), .count(1'b1), .clk(clock_1_out), .carry(counter_1_carry), .Q(counter_1_q));  // open: clr, load, D
  Register register_1 (.D(in_3), .en(in_4), .clk(clock_1_out), .Q(register_1_q));  // open: clr
  Multiplexer #(.select(2)) multiplexer_1 ();  // open: in0, in1, in2, in3, out, sel
  assign controlled_buffer_1_out = counter_1_carry ? multiplier_1_out : 8'bz;  // Controlled_Buffer controlled_buffer_1
  not not_1 (not_1_out, counter_1_carry);
  assign controlled_buffer_1_out = not_1_out ? {8{1'b0}} : 8'bz;  // Controlled_Buffer controlled_buffer_2
  Register register_2 (.D(adder_1_out), .en(in_2), .clk(clock_1_out), .Q(register_2_q));  // open: clr
  Multiplier multiplier_1 (.a(8'h2), .b(register_1_q), .out(multiplier_1_out));  // open: cin, cout
  // Probe on adder_1_out
  RAM ram_1 (.addr(counter_1_q), .oe(in_5), .clk(clock_1_out), .dout(ram_1_dout));  // open: we, din
  Adder adder_1 (.a(controlled_buffer_1_out), .b(register_2_q), .out(adder_1_out));  // open: cin, cout
  Adder adder_2 (.a(register_2_q), .b(counter_1_q), .out(adder_2_out));  // open: cin, cout
  Divider divider_1 (.a(in_8), .b(in_10), .out(out_11));  // open: upper, rem
  RAM ram_2 (.addr(adder_2_out), .oe(in_2), .clk(clock_1_out), .dout(ram_2_dout));  // open: we, din
  // Probe on adder_2_out
  // Probe on ram_1_dout
  // Probe on ram_2_dout
  Register register_3 (.D(ram_1_dout), .en(in_6), .clk(clock_1_out), .Q(register_3_q), .clr(in_7));
  Adder adder_3 (.a(adder_2_out), .b(register_1_q), .out(adder_3_out));  // open: cin, cout
  Decoder #(.select(2)) decoder_1 (
    .out0(decoder_1_out0), .out1(decoder_1_out1), .out2(decoder_1_out2), .out3(decoder_1_out3), .sel(in_9));  // open: en
  // Probe on register_3_q
  RAM ram_3 (.addr(adder_3_out));  // open: we, oe, clk, din, dout
  // Probe on adder_3_out

  // Notes on the sheet:
  //   in_3: initial=0x10
  //   in_4: initial=0x1
  //   in_2: initial=0x1
  //   in_7: initial=0x1
endmodule

module Ldecoder (
  input  first,
  input  second,
  input  third,
  input  fourth,
  output a11,
  output a12,
  output a21,
  output a22,
  output a31,
  output a32,
  output a41,
  output a42,
  output a51,
  output a52,
  output a61,
  output a62,
  output a71,
  output a72,
  output a81,
  output a82
);

  wire not_1_out, not_2_out, not_3_out, not_4_out, not_5_out, not_6_out, not_7_out, not_8_out, not_9_out,
       not_10_out, not_11_out, not_12_out, not_13_out, not_14_out, not_15_out, not_16_out, not_17_out,
       not_18_out, not_19_out, not_20_out, not_21_out, not_22_out, not_23_out, not_24_out, not_25_out,
       not_26_out, not_27_out, not_28_out, not_29_out, not_30_out, not_31_out, not_32_out;

  not not_1 (not_1_out, first);
  not not_2 (not_2_out, first);
  not not_3 (not_3_out, first);
  not not_4 (not_4_out, first);
  not not_5 (not_5_out, first);
  not not_6 (not_6_out, first);
  not not_7 (not_7_out, first);
  not not_8 (not_8_out, first);
  not not_9 (not_9_out, second);
  not not_10 (not_10_out, third);
  not not_11 (not_11_out, second);
  not not_12 (not_12_out, third);
  not not_13 (not_13_out, third);
  not not_14 (not_14_out, third);
  not not_15 (not_15_out, second);
  not not_16 (not_16_out, second);
  not not_17 (not_17_out, second);
  not not_18 (not_18_out, third);
  not not_19 (not_19_out, second);
  not not_20 (not_20_out, third);
  not not_21 (not_21_out, third);
  not not_22 (not_22_out, third);
  not not_23 (not_23_out, second);
  not not_24 (not_24_out, second);
  not not_25 (not_25_out, fourth);
  not not_26 (not_26_out, fourth);
  not not_27 (not_27_out, fourth);
  not not_28 (not_28_out, fourth);
  not not_29 (not_29_out, fourth);
  not not_30 (not_30_out, fourth);
  not not_31 (not_31_out, fourth);
  not not_32 (not_32_out, fourth);
  and and_1 (a11, not_1_out, not_9_out, not_10_out, not_25_out);
  and and_2 (a12, first, not_11_out, not_12_out, not_26_out);
  and and_3 (a21, not_2_out, second, not_13_out, not_27_out);
  and and_4 (a22, first, second, not_14_out, not_28_out);
  and and_5 (a31, not_3_out, not_15_out, third, not_29_out);
  and and_6 (a32, first, not_16_out, third, not_30_out);
  and and_7 (a41, not_4_out, second, third, not_31_out);
  and and_8 (a42, first, second, third, not_32_out);
  and and_9 (a51, not_5_out, not_17_out, not_18_out, fourth);
  and and_10 (a52, first, not_19_out, not_20_out, fourth);
  and and_11 (a61, not_6_out, second, not_21_out, fourth);
  and and_12 (a62, first, second, not_22_out, fourth);
  and and_13 (a71, not_7_out, not_23_out, third, fourth);
  and and_14 (a72, first, not_24_out, third, fourth);
  and and_15 (a81, not_8_out, second, third, fourth);
  and and_16 (a82, first, second, third, fourth);
endmodule
